# Fritzing sketch p1_Flexy_Meter (saved by Fritzing 1.0.7)
circuit board: 7.68862cm x 2.85426cm
breadboards: 1

parts:
  U1 = Heltec CubeCell 1/2AA Node (HTCC-AB02A) [part_number=HTCC-AB02A]
  JP1 = Header 6 [package=molex-1x6-ra]
  Q2 = NPN-Transistor [package="TO92 [THT]"]
  R2 = Resistor [tolerance=±5% resistance=10k power=0W package="2512 [SMD]"]
  R3 = Resistor [tolerance=±5% resistance=10k power=0W package="2512 [SMD]"]

nets:
  N1: U1.pin_2, U1.pin_20, JP1.P3_GND, JP1.P6_GND, Q2.C
  N2: U1.pin_3, U1.pin_21
  N3: U1.pin_4, Q2.E, R3.Pin_0
  N4: U1.pin_15, U1.pin_17
  N5: U1.pin_16, U1.pin_18
  N6: U1.pin_33, U1.pin_35
  N7: U1.pin_34, U1.pin_36
  N8: JP1.P1_5V, JP1.P2_data_request, R2.Pin_1, R3.Pin_1
  N9: JP1.P5_Data, Q2.B, R2.Pin_0

notes:
  P1 meter
  GND
  +5V
  REQ
  DATA
  BS170
  R1 10K
  R2 10K
  Cube Cell HTCC-AB02A

custom parts:
  Heltec CubeCell 1/2AA Node (HTCC-AB02A): Heltec CubeCell HTCC-AB02A 1/2AA LoRaWAN node with ASR6501 processor and SX1262 RF transceiver, featuring 36 pins including SPI, I2C, UART, ADC, PWM, and LoRa radio connections.
  Header 6: Header 6 Standard 6-pin 0.1 header. Use with straight break away headers (SKU : PRT-00116), right angle break away headers (PRT-00553), swiss pins (PRT-00743), machine pins (PRT-00117), and female headers (PRT-00115). Molex polarized connector foot print use with SKU : PRT-08094 with associated crimp pins and housings. NOTES ON THE VARIANTS LOCK and LOCK_LONGPADS... This footprint was designed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
